// Logisim project Fahmida_Akter_Nourin_2031741642.circ as structural Verilog: 3 circuits, main circuit main
module main (
  input  B3,
  input  B2,
  input  B1,
  input  B0,
  input  A0,
  input  A1,
  input  in_7,
  input  in_8,
  input  A2,
  input  in_10,
  input  A3,
  input  in_12
);

  wire and_ic_7408_1_m0, and_ic_7408_1_m1, and_ic_7408_1_m2, and_ic_7408_1_m3, and_ic_7408_2_m0,
       and_ic_7408_2_m1, and_ic_7408_2_m2, and_ic_7408_2_m3, and_ic_7408_3_m0, and_ic_7408_3_m1,
       and_ic_7408_3_m2, and_ic_7408_3_m3, and_ic_7408_4_m1, and_ic_7408_4_m2, and_ic_7408_4_m3,
       fulladder_2_c3, fulladder_2_s1, fulladder_2_s2, fulladder_2_s3, fulladder_3_c3, fulladder_3_s1,
       fulladder_3_s2, fulladder_3_s3, S0, S1, S2, S3, S4, S5, S6, S7;

  AND_IC_7408 and_ic_7408_1 (
    .A0(A3), .B0(B0), .A1(A3), .B1(B1), .A2(A3), .B2(B2), .A3(A3), .B3(B3), .M0(and_ic_7408_1_m0),
    .M1(and_ic_7408_1_m1), .M2(and_ic_7408_1_m2), .M3(and_ic_7408_1_m3));
  AND_IC_7408 and_ic_7408_2 (
    .A0(A1), .B0(B0), .A1(A1), .B1(B1), .A2(A1), .B2(B2), .A3(A1), .B3(B3), .M0(and_ic_7408_2_m0),
    .M1(and_ic_7408_2_m1), .M2(and_ic_7408_2_m2), .M3(and_ic_7408_2_m3));
  AND_IC_7408 and_ic_7408_3 (
    .A0(A2), .B0(B0), .A1(A2), .B1(B1), .A2(A2), .B2(B2), .A3(A2), .B3(B3), .M0(and_ic_7408_3_m0),
    .M1(and_ic_7408_3_m1), .M2(and_ic_7408_3_m2), .M3(and_ic_7408_3_m3));
  FullAdder fulladder_1 (
    .A0(fulladder_2_s1), .B0(and_ic_7408_1_m0), .C0(in_12), .A1(fulladder_2_s2), .B1(and_ic_7408_1_m1),
    .A2(fulladder_2_s3), .B2(and_ic_7408_1_m2), .A3(fulladder_2_c3), .B3(and_ic_7408_1_m3), .S0(S3), .S1(S4),
    .S2(S5), .S3(S6), .C3(S7));
  FullAdder fulladder_2 (
    .A0(fulladder_3_s1), .B0(and_ic_7408_3_m0), .C0(in_10), .A1(fulladder_3_s2), .B1(and_ic_7408_3_m1),
    .A2(fulladder_3_s3), .B2(and_ic_7408_3_m2), .A3(fulladder_3_c3), .B3(and_ic_7408_3_m3), .S0(S2),
    .S1(fulladder_2_s1), .S2(fulladder_2_s2), .S3(fulladder_2_s3), .C3(fulladder_2_c3));
  FullAdder fulladder_3 (
    .A0(and_ic_7408_4_m1), .B0(and_ic_7408_2_m0), .C0(in_8), .A1(and_ic_7408_4_m2), .B1(and_ic_7408_2_m1),
    .A2(and_ic_7408_4_m3), .B2(and_ic_7408_2_m2), .A3(and_ic_7408_2_m3), .B3(in_7), .S0(S1),
    .S1(fulladder_3_s1), .S2(fulladder_3_s2), .S3(fulladder_3_s3), .C3(fulladder_3_c3));
  AND_IC_7408 and_ic_7408_4 (
    .A0(A0), .B0(B0), .A1(A0), .B1(B1), .A2(A0), .B2(B2), .A3(A0), .B3(B3), .M0(S0), .M1(and_ic_7408_4_m1),
    .M2(and_ic_7408_4_m2), .M3(and_ic_7408_4_m3));
endmodule

module FullAdder (
  input  A0,
  input  B0,
  input  C0,
  input  A1,
  input  B1,
  input  A2,
  input  B2,
  input  A3,
  input  B3,
  output S0,
  output S1,
  output S2,
  output S3,
  output C3
);

  wire and_1_out, and_2_out, and_3_out, and_4_out, and_5_out, and_6_out, and_7_out, and_8_out, C0_t, C1, C2,
       xor_1_out, xor_2_out, xor_3_out, xor_4_out;

  xor xor_1 (xor_1_out, A0, B0);
  and and_1 (and_1_out, A0, B0);
  xor xor_2 (xor_2_out, A1, B1);
  and and_2 (and_2_out, A1, B1);
  xor xor_3 (xor_3_out, A2, B2);
  and and_3 (and_3_out, A2, B2);
  xor xor_4 (xor_4_out, A3, B3);
  and and_4 (and_4_out, A3, B3);
  xor xor_5 (S0, xor_1_out, C0);
  and and_5 (and_5_out, C0, xor_1_out);
  xor xor_6 (S1, xor_2_out, C0_t);
  and and_6 (and_6_out, C0_t, xor_2_out);
  xor xor_7 (S2, xor_3_out, C1);
  and and_7 (and_7_out, C1, xor_3_out);
  xor xor_8 (S3, xor_4_out, C2);
  and and_8 (and_8_out, C2, xor_4_out);
  or or_1 (C0_t, and_5_out, and_1_out);
  or or_2 (C1, and_6_out, and_2_out);
  or or_3 (C2, and_7_out, and_3_out);
  or or_4 (C3, and_8_out, and_4_out);
endmodule

module AND_IC_7408 (
  input  A0,
  input  B0,
  input  A1,
  input  B1,
  input  A2,
  input  B2,
  input  A3,
  input  B3,
  output M0,
  output M1,
  output M2,
  output M3
);

  and and_1 (M0, A0, B0);
  and and_2 (M1, A1, B1);
  and and_3 (M2, A2, B2);
  and and_4 (M3, A3, B3);
endmodule
